// Logisim project CPU.circ as structural Verilog
module HalfSum (
  input  a,
  input  b,
  output CarryOut,
  output Sum
);

  and and_1 (CarryOut, a, b);
  xor xor_1 (Sum, b, a);
endmodule

module FullSum (
  input  a,
  input  b,
  input  c,
  output Sum,
  output CarryOut
);

  wire halfsum_1_carryout, halfsum_1_sum, halfsum_2_carryout;

  HalfSum halfsum_1 (.a(a), .b(b), .CarryOut(halfsum_1_carryout), .Sum(halfsum_1_sum));
  HalfSum halfsum_2 (.a(c), .b(halfsum_1_sum), .CarryOut(halfsum_2_carryout), .Sum(Sum));
  or or_1 (CarryOut, halfsum_2_carryout, halfsum_1_carryout);
endmodule

module Sum (
  input  [3:0] in_1,
  input  CarryIn,
  input  [3:0] in_3,
  output [4:0] out_4
);

  wire fullsum_1_carryout, fullsum_2_carryout, fullsum_3_carryout;

  // Probe on in_1
  FullSum fullsum_1 (.a(in_3[0]), .b(in_1[0]), .c(CarryIn), .Sum(out_4[0]), .CarryOut(fullsum_1_carryout));
  FullSum fullsum_2 (.a(in_3[1]), .b(in_1[1]), .c(fullsum_1_carryout), .Sum(out_4[1]), .CarryOut(fullsum_2_carryout));
  FullSum fullsum_3 (.a(in_3[2]), .b(in_1[2]), .c(fullsum_2_carryout), .Sum(out_4[2]), .CarryOut(fullsum_3_carryout));
  FullSum fullsum_4 (.a(in_3[3]), .b(in_1[3]), .c(fullsum_3_carryout), .Sum(out_4[3]), .CarryOut(out_4[4]));
  // Probe on in_3
  // Probe on out_4
endmodule

module ULA (
  input  [15:0] A,
  input  in_2,
  input  in_3,
  input  [15:0] B,
  input  in_5,
  input  [3:0] \Operação ,
  output [15:0] out_7
);

  wire and_1_out, and_2_out, not_1_out, or_1_out;
  wire [15:0] outAnd, outDiv, outLeftShift, outMult, outNAND, outNOR, outOr, outRightShift, outSub, outSum,
       outXOR;

  Multiplexer #(.select(4), .width(16)) multiplexer_1 (
    .in0(outSum), .in2(outOr), .in4(outMult), .in6(outNAND), .in8(outDiv), .in10(outAnd), .in12(outSub),
    .in13(outRightShift), .in14(outNOR), .in15(outLeftShift), .out(out_7), .sel(\Operação ));  // open: in1, in3, in5, in7, in9, in11, en
  not not_1 (not_1_out, in_3);
  and and_1 (and_1_out, in_2, not_1_out);
  and and_2 (and_2_out, in_3, in_5);
  or or_1 (or_1_out, and_1_out, and_2_out);
  Adder #(.width(16)) adder_1 (.a(A), .b(B), .out(outSum));  // open: cin, cout
  Subtractor #(.width(16)) subtractor_1 (.a(A), .b(B), .out(outSub));  // open: bin, bout
  Multiplier #(.width(16)) multiplier_1 (.a(A), .b(B), .out(outMult));  // open: cin, cout
  Divider #(.width(16)) divider_1 (.a(A), .b(B), .out(outDiv));  // open: upper, rem
  assign outAnd = A & B;  // AND_Gate and_3, 16 bits wide
  assign outOr = A | B;  // OR_Gate or_2, 16 bits wide
  assign outNAND = ~(A & B);  // NAND_Gate nand_1, 16 bits wide
  assign outXOR = A ^ B;  // XOR_Gate xor_1, 16 bits wide
  Shifter #(.width(16)) shifter_1 (.in(A), .\dist (B[3:0]), .out(outLeftShift));
  Shifter #(.width(16), .shift("lr")) shifter_2 (.in(A), .\dist (B[3:0]), .out(outRightShift));
endmodule
